# Fritzing sketch Anemone Prototype Shield with ICSP (saved by Fritzing 0.9.3b)
breadboards: 1

parts:
  Arduino_YÚN = Arduino Yun
  Adafruit_Prototype_Shield = Adafruit Proto Shield for Arduino Kit - v.5

nets (from the breadboard view):
  N1: Arduino_YÚN.ICSP_MISO, Arduino_YÚN.D12/MISO, Adafruit_Prototype_Shield.D12
  5V: Arduino_YÚN.5V, Adafruit_Prototype_Shield.+5V
  N2: Arduino_YÚN.ICSP_SCK, Arduino_YÚN.D13/SCK, Adafruit_Prototype_Shield.D13
  N3: Arduino_YÚN.ICSP_MOSI, Arduino_YÚN.D11_PWM/MOSI, Adafruit_Prototype_Shield.D11
  N4: Arduino_YÚN.RESET, Adafruit_Prototype_Shield.RESET
  GND: Arduino_YÚN.GND, Adafruit_Prototype_Shield.GND
  N5: Arduino_YÚN.D8, Adafruit_Prototype_Shield.D8
  N6: Arduino_YÚN.D9_PWM, Adafruit_Prototype_Shield.D9
  N7: Arduino_YÚN.D10_PWM/SS, Adafruit_Prototype_Shield.D10
  N8: Arduino_YÚN.AREF, Adafruit_Prototype_Shield.AREF
  N9: Arduino_YÚN.D0/RX, Adafruit_Prototype_Shield.D0
  N10: Arduino_YÚN.D1/TX, Adafruit_Prototype_Shield.D1
  N11: Arduino_YÚN.D2, Adafruit_Prototype_Shield.D2
  N12: Arduino_YÚN.D3_PWM, Adafruit_Prototype_Shield.D3
  N13: Arduino_YÚN.D4, Adafruit_Prototype_Shield.D4
  N14: Arduino_YÚN.D5_PWM, Adafruit_Prototype_Shield.D5
  N15: Arduino_YÚN.D6_PWM, Adafruit_Prototype_Shield.D6
  N16: Arduino_YÚN.D7, Adafruit_Prototype_Shield.D7
  3V3: Arduino_YÚN.3V3, Adafruit_Prototype_Shield.3.3V

custom parts:
  Adafruit Proto Shield for Arduino Kit - v.5: Arduino prototyping shield designed by Adafruit Industries
