# Fritzing sketch Anemone Tentacle Display Board (saved by Fritzing 0.9.3b)
perfboards: 1
stripboards: 1

parts:
  Arduino_TFT_Display = 1.8" TFT Display with uSD
  S2 = Momentary Switch [package=ksa_sealed_tac_switch]
  R4 = Resistor [tolerance=±5% resistance=22 package=THT]
  J2 = Piezo Speaker
  Q1 = TRANSISTOR_PNP [part_number="T5 9012" package=to-92]

nets:
  N1: Arduino_TFT_Display.BL, Arduino_TFT_Display.MISO, S2.4, J2.pin1, Q1.C
  N2: R4.Pin_1, Q1.B
  N3: J2.pin2, Q1.E

notes:
  Buzzer YL-44
  Cloud button
  Arduino TFT
  Display

custom parts:
  1.8" TFT Display with uSD: 1.8" TFT Display with SPI control and MicroSD card
