# Fritzing sketch Anemone Tentacle Minimal (saved by Fritzing 0.9.3b)
breadboards: 1

parts:
  Arduino_TFT_Display = 1.8" TFT Display with uSD
  S2 = Momentary Switch [package=ksa_sealed_tac_switch]
  U4 = TLP621 [package=THT]
  R4 = Resistor [tolerance=±5% resistance=220 package=THT]
  R2 = Resistor [tolerance=±5% resistance=10k package=THT]
  Arduino_YÚN = Arduino Yun

nets (from the breadboard view):
  N1: Arduino_TFT_Display.BL, U4.Pin_2, R2.Pin_0, Arduino_YÚN.GND
  N2: Arduino_TFT_Display.MISO, S2.2, U4.Pin_4, Arduino_YÚN.5V
  N3: Arduino_TFT_Display.SCK, Arduino_YÚN.D8
  N4: Arduino_TFT_Display.MOSI, Arduino_YÚN.D9_PWM
  N5: Arduino_TFT_Display.CS, Arduino_YÚN.D4
  N6: Arduino_TFT_Display.SDCS, Arduino_YÚN.D10_PWM/SS
  N7: Arduino_TFT_Display.D/C, Arduino_YÚN.ICSP_MOSI
  N8: Arduino_TFT_Display.RST, Arduino_YÚN.ICSP_SCK
  N9: Arduino_TFT_Display.VCC, Arduino_YÚN.ICSP_MISO
  N10: Arduino_TFT_Display.GND, U4.Pin_3
  N11: S2.4, R2.Pin_1, Arduino_YÚN.D6_PWM
  N12: U4.Pin_1, R4.Pin_0
  N13: R4.Pin_1, Arduino_YÚN.D2

notes:
  Cloud button (S2)
  Arduino TFT
  Display
  Red = Vcc 5V
  Pink = Vcc 3.3V
  Black = GND

custom parts:
  1.8" TFT Display with uSD: 1.8" TFT Display with SPI control and MicroSD card
