# Fritzing sketch Anemone Tentacle Build 1 Tentacle Shield (saved by Fritzing 0.9.3b)
breadboards: 1

parts:
  Adafruit_Prototype_Shield = Adafruit Proto Shield for Arduino Kit - v.5
  U2 = TLP621 [package=THT]
  R1 = Resistor [tolerance=±5% resistance=220 package=THT]
  R2 = Resistor [tolerance=±5% resistance=10k package=THT]
  U1 = TLP621 [package=THT]
  R5 = Resistor [tolerance=±5% resistance=10k package=THT]
  R6 = Resistor [tolerance=±5% resistance=220 package=THT]

nets (from the breadboard view):
  N1: Adafruit_Prototype_Shield.GND, Adafruit_Prototype_Shield.P$4, Adafruit_Prototype_Shield.P$5, U2.Pin_2, R2.Pin_1, U1.Pin_2, R5.Pin_1
  N2: Adafruit_Prototype_Shield.D13, R6.Pin_1
  N3: Adafruit_Prototype_Shield.D2, R1.Pin_1
  N4: Adafruit_Prototype_Shield.D6, R5.Pin_0
  N5: Adafruit_Prototype_Shield.D7, R2.Pin_0
  N6: Adafruit_Prototype_Shield.+5V, Adafruit_Prototype_Shield.P$11, U2.Pin_4
  N7: Adafruit_Prototype_Shield.3.3V, U1.Pin_4
  N8: U2.Pin_1, R1.Pin_0
  N9: U1.Pin_1, R6.Pin_0

custom parts:
  Adafruit Proto Shield for Arduino Kit - v.5: Arduino prototyping shield designed by Adafruit Industries
