# Fritzing sketch Anemone Tentacle Build 4 Back Button (saved by Fritzing 0.9.3b)
breadboards: 1

parts:
  Arduino_YÚN = Arduino Yun
  Adafruit_Prototype_Shield = Adafruit Proto Shield for Arduino Kit - v.5
  S1 = Momentary Switch [package=ksa_sealed_tac_switch]
  U2 = TLP621 [package=THT]
  R1 = Resistor [tolerance=±5% resistance=220 package=THT]
  R2 = Resistor [tolerance=±5% resistance=10k package=THT]
  U1 = TLP621 [package=THT]
  R5 = Resistor [tolerance=±5% resistance=10k package=THT]
  R6 = Resistor [tolerance=±5% resistance=220 package=THT]

nets (from the breadboard view):
  N1: Arduino_YÚN.ICSP_MISO, Arduino_YÚN.D12/MISO, Adafruit_Prototype_Shield.D12
  5V: Arduino_YÚN.5V, Adafruit_Prototype_Shield.+5V, Adafruit_Prototype_Shield.P$4#203, Adafruit_Prototype_Shield.P$11, S1.1, U2.Pin_4
  N2: Arduino_YÚN.ICSP_SCK, Arduino_YÚN.D13/SCK, Adafruit_Prototype_Shield.D13, R6.Pin_1
  N3: Arduino_YÚN.ICSP_MOSI, Arduino_YÚN.D11_PWM/MOSI, Adafruit_Prototype_Shield.D11
  N4: Arduino_YÚN.RESET, Adafruit_Prototype_Shield.RESET
  GND: Arduino_YÚN.GND, Adafruit_Prototype_Shield.GND, Adafruit_Prototype_Shield.P$4#213, Adafruit_Prototype_Shield.P$5, U2.Pin_2, R2.Pin_1, U1.Pin_2, R5.Pin_1
  N5: Arduino_YÚN.D8, Adafruit_Prototype_Shield.D8
  N6: Arduino_YÚN.D9_PWM, Adafruit_Prototype_Shield.D9
  N7: Arduino_YÚN.D10_PWM/SS, Adafruit_Prototype_Shield.D10
  N8: Arduino_YÚN.AREF, Adafruit_Prototype_Shield.AREF
  N9: Arduino_YÚN.D0/RX, Adafruit_Prototype_Shield.D0
  N10: Arduino_YÚN.D1/TX, Adafruit_Prototype_Shield.D1
  N11: Arduino_YÚN.D2, Adafruit_Prototype_Shield.D2, R1.Pin_1
  N12: Arduino_YÚN.D3_PWM, Adafruit_Prototype_Shield.D3
  N13: Arduino_YÚN.D4, Adafruit_Prototype_Shield.D4
  N14: Arduino_YÚN.D5_PWM, Adafruit_Prototype_Shield.D5
  N15: Arduino_YÚN.D6_PWM, Adafruit_Prototype_Shield.D6, R5.Pin_0
  N16: Arduino_YÚN.D7, Adafruit_Prototype_Shield.D7, S1.4, R2.Pin_0
  3V3: Arduino_YÚN.3V3, Adafruit_Prototype_Shield.3.3V, U1.Pin_4
  N17: U2.Pin_1, R1.Pin_0
  N18: U1.Pin_1, R6.Pin_0

notes:
  Back button

custom parts:
  Adafruit Proto Shield for Arduino Kit - v.5: Arduino prototyping shield designed by Adafruit Industries
